// Logisim project TP2_Mick_Forward.circ as structural Verilog: 20 circuits, main circuit main
module main (
);

  wire bcd_7s_1_a, bcd_7s_1_b, bcd_7s_1_c, bcd_7s_1_d, bcd_7s_1_e, bcd_7s_1_f, bcd_7s_1_g, bcd_7s_2_a,
       bcd_7s_2_b, bcd_7s_2_c, bcd_7s_2_d, bcd_7s_2_e, bcd_7s_2_f, bcd_7s_2_g, bcd_7s_3_a, bcd_7s_3_b,
       bcd_7s_3_c, bcd_7s_3_d, bcd_7s_3_e, bcd_7s_3_f, bcd_7s_3_g, bcd_7s_4_a, bcd_7s_4_b, bcd_7s_4_c,
       bcd_7s_4_d, bcd_7s_4_e, bcd_7s_4_f, bcd_7s_4_g, bcd_7s_5_a, bcd_7s_5_b, bcd_7s_5_c, bcd_7s_5_d,
       bcd_7s_5_e, bcd_7s_5_f, bcd_7s_5_g, bcd_7s_6_a, bcd_7s_6_b, bcd_7s_6_c, bcd_7s_6_d, bcd_7s_6_e,
       bcd_7s_6_f, bcd_7s_6_g, bcd_7s_7_a, bcd_7s_7_b, bcd_7s_7_c, bcd_7s_7_d, bcd_7s_7_e, bcd_7s_7_f,
       bcd_7s_7_g, bcd_7s_8_a, bcd_7s_8_b, bcd_7s_8_c, bcd_7s_8_d, bcd_7s_8_e, bcd_7s_8_f, bcd_7s_8_g,
       bcd_7s_9_a, bcd_7s_9_b, bcd_7s_9_c, bcd_7s_9_d, bcd_7s_9_e, bcd_7s_9_f, bcd_7s_9_g, bcd_7s_10_a,
       bcd_7s_10_b, bcd_7s_10_c, bcd_7s_10_d, bcd_7s_10_e, bcd_7s_10_f, bcd_7s_10_g, bcd_7s_11_a,
       bcd_7s_11_b, bcd_7s_11_c, bcd_7s_11_d, bcd_7s_11_e, bcd_7s_11_f, bcd_7s_11_g, bcd_7s_12_a,
       bcd_7s_12_b, bcd_7s_12_c, bcd_7s_12_d, bcd_7s_12_e, bcd_7s_12_f, bcd_7s_12_g, bcd_7s_13_a,
       bcd_7s_13_b, bcd_7s_13_c, bcd_7s_13_d, bcd_7s_13_e, bcd_7s_13_f, bcd_7s_13_g,
       cache_1_ld_to_mem_contrl, cache_1_ready_to_up, cache_1_sd_to_mem_contrl, clock_1_out,
       Horloge_1_clk_out, Memory_controller_1_clk_to_mem_data, Memory_controller_1_ld_to_mem_data,
       Memory_controller_1_ready_to_cache, Memory_controller_1_sd_to_mem_data, Microprocesseur_1_ld_to_cache,
       Microprocesseur_1_sd_to_cache;
  wire [3:0] Periph_listener_1_address_000_value_3to0, Periph_listener_1_address_000_value_7to4,
       Periph_listener_1_address_000_value_bto8, Periph_listener_1_address_001_value_3to0,
       Periph_listener_1_address_001_value_7to4, Periph_listener_1_address_001_value_bto8,
       Periph_listener_1_address_002_value_3to0, Periph_listener_1_address_002_value_7to4,
       Periph_listener_1_address_002_value_bto8;
  wire [11:0] cache_1_address_to_mem_contrl, cache_1_ld_data_to_up, cache_1_sd_data_to_mem_contrl,
       Memoire_des_donnees_dout, Memoire_instructions_dout, Memory_controller_1_address_to_mem_data,
       Memory_controller_1_data_to_mem_data, Memory_controller_1_ld_data_to_cache,
       Microprocesseur_1_address_to_cache, Microprocesseur_1_address_to_mem_instr,
       Microprocesseur_1_sd_data_to_cache;

  Clock clock_1 (.out(clock_1_out));
  _7_Segment_Display u_7_segment_display_1 (
    .g(bcd_7s_1_g), .f(bcd_7s_1_f), .a(bcd_7s_1_a), .b(bcd_7s_1_b), .e(bcd_7s_1_e), .d(bcd_7s_1_d),
    .c(bcd_7s_1_c));  // open: dp
  BCD_7S bcd_7s_1 (
    .C(bcd_7s_1_c), .E(bcd_7s_1_e), .G(bcd_7s_1_g), .A(bcd_7s_1_a), .D(bcd_7s_1_d), .F(bcd_7s_1_f),
    .B(bcd_7s_1_b));  // open: Data
  // Binary_to_BCD_converter #(.binvalue(12)) binary_to_bcd_converter_1: pin names not known
  _7_Segment_Display u_7_segment_display_2 (
    .g(bcd_7s_2_g), .f(bcd_7s_2_f), .a(bcd_7s_2_a), .b(bcd_7s_2_b), .e(bcd_7s_2_e), .d(bcd_7s_2_d),
    .c(bcd_7s_2_c));  // open: dp
  BCD_7S bcd_7s_2 (
    .C(bcd_7s_2_c), .E(bcd_7s_2_e), .G(bcd_7s_2_g), .A(bcd_7s_2_a), .D(bcd_7s_2_d), .F(bcd_7s_2_f),
    .B(bcd_7s_2_b));  // open: Data
  Microprocesseur Microprocesseur_1 (
    .ld_data_from_cache(cache_1_ld_data_to_up), .ready_from_cache(cache_1_ready_to_up),
    .data_from_mem_instr(Memoire_instructions_dout), .Clk(Horloge_1_clk_out),
    .sd_data_to_cache(Microprocesseur_1_sd_data_to_cache),
    .address_to_cache(Microprocesseur_1_address_to_cache), .ld_to_cache(Microprocesseur_1_ld_to_cache),
    .sd_to_cache(Microprocesseur_1_sd_to_cache), .address_to_mem_instr(Microprocesseur_1_address_to_mem_instr));
  _7_Segment_Display u_7_segment_display_3 (
    .g(bcd_7s_3_g), .f(bcd_7s_3_f), .a(bcd_7s_3_a), .b(bcd_7s_3_b), .e(bcd_7s_3_e), .d(bcd_7s_3_d),
    .c(bcd_7s_3_c));  // open: dp
  _7_Segment_Display u_7_segment_display_4 (
    .g(bcd_7s_4_g), .f(bcd_7s_4_f), .a(bcd_7s_4_a), .b(bcd_7s_4_b), .e(bcd_7s_4_e), .d(bcd_7s_4_d),
    .c(bcd_7s_4_c));  // open: dp
  BCD_7S bcd_7s_3 (
    .C(bcd_7s_3_c), .E(bcd_7s_3_e), .G(bcd_7s_3_g), .A(bcd_7s_3_a), .D(bcd_7s_3_d), .F(bcd_7s_3_f),
    .B(bcd_7s_3_b));  // open: Data
  BCD_7S bcd_7s_4 (
    .C(bcd_7s_4_c), .E(bcd_7s_4_e), .G(bcd_7s_4_g), .A(bcd_7s_4_a), .D(bcd_7s_4_d), .F(bcd_7s_4_f),
    .B(bcd_7s_4_b));  // open: Data
  Horloge Horloge_1 (
    .Clk_in(clock_1_out), .Data(Microprocesseur_1_sd_data_to_cache),
    .Listen_address(Microprocesseur_1_address_to_cache), .En(Microprocesseur_1_sd_to_cache),
    .Clk_out(Horloge_1_clk_out));  // open: Count
  _7_Segment_Display u_7_segment_display_5 (
    .g(bcd_7s_5_g), .f(bcd_7s_5_f), .a(bcd_7s_5_a), .b(bcd_7s_5_b), .e(bcd_7s_5_e), .d(bcd_7s_5_d),
    .c(bcd_7s_5_c));  // open: dp
  _7_Segment_Display u_7_segment_display_6 (
    .g(bcd_7s_6_g), .f(bcd_7s_6_f), .a(bcd_7s_6_a), .b(bcd_7s_6_b), .e(bcd_7s_6_e), .d(bcd_7s_6_d),
    .c(bcd_7s_6_c));  // open: dp
  BCD_7S bcd_7s_5 (
    .Data(Periph_listener_1_address_002_value_bto8), .C(bcd_7s_5_c), .E(bcd_7s_5_e), .G(bcd_7s_5_g),
    .A(bcd_7s_5_a), .D(bcd_7s_5_d), .F(bcd_7s_5_f), .B(bcd_7s_5_b));
  _7_Segment_Display u_7_segment_display_7 (
    .g(bcd_7s_7_g), .f(bcd_7s_7_f), .a(bcd_7s_7_a), .b(bcd_7s_7_b), .e(bcd_7s_7_e), .d(bcd_7s_7_d),
    .c(bcd_7s_7_c));  // open: dp
  BCD_7S bcd_7s_6 (
    .Data(Periph_listener_1_address_002_value_7to4), .C(bcd_7s_6_c), .E(bcd_7s_6_e), .G(bcd_7s_6_g),
    .A(bcd_7s_6_a), .D(bcd_7s_6_d), .F(bcd_7s_6_f), .B(bcd_7s_6_b));
  Cache cache_1 (
    .Ready_from_mem_contrl(Memory_controller_1_ready_to_cache), .Clk(Horloge_1_clk_out),
    .ld_from_up(Microprocesseur_1_ld_to_cache), .sd_from_up(Microprocesseur_1_sd_to_cache),
    .Address_from_up(Microprocesseur_1_address_to_cache),
    .ld_data_from_mem_contrl(Memory_controller_1_ld_data_to_cache),
    .sd_data_from_up(Microprocesseur_1_sd_data_to_cache), .Ready_to_up(cache_1_ready_to_up),
    .ld_to_mem_contrl(cache_1_ld_to_mem_contrl), .sd_to_mem_contrl(cache_1_sd_to_mem_contrl),
    .Address_to_mem_contrl(cache_1_address_to_mem_contrl), .ld_data_to_up(cache_1_ld_data_to_up),
    .sd_data_to_mem_contrl(cache_1_sd_data_to_mem_contrl));
  _7_Segment_Display u_7_segment_display_8 (
    .g(bcd_7s_8_g), .f(bcd_7s_8_f), .a(bcd_7s_8_a), .b(bcd_7s_8_b), .e(bcd_7s_8_e), .d(bcd_7s_8_d),
    .c(bcd_7s_8_c));  // open: dp
  BCD_7S bcd_7s_7 (
    .Data(Periph_listener_1_address_002_value_3to0), .C(bcd_7s_7_c), .E(bcd_7s_7_e), .G(bcd_7s_7_g),
    .A(bcd_7s_7_a), .D(bcd_7s_7_d), .F(bcd_7s_7_f), .B(bcd_7s_7_b));
  BCD_7S bcd_7s_8 (
    .Data(Periph_listener_1_address_001_value_bto8), .C(bcd_7s_8_c), .E(bcd_7s_8_e), .G(bcd_7s_8_g),
    .A(bcd_7s_8_a), .D(bcd_7s_8_d), .F(bcd_7s_8_f), .B(bcd_7s_8_b));
  _7_Segment_Display u_7_segment_display_9 (
    .g(bcd_7s_9_g), .f(bcd_7s_9_f), .a(bcd_7s_9_a), .b(bcd_7s_9_b), .e(bcd_7s_9_e), .d(bcd_7s_9_d),
    .c(bcd_7s_9_c));  // open: dp
  _7_Segment_Display u_7_segment_display_10 (
    .g(bcd_7s_10_g), .f(bcd_7s_10_f), .a(bcd_7s_10_a), .b(bcd_7s_10_b), .e(bcd_7s_10_e), .d(bcd_7s_10_d),
    .c(bcd_7s_10_c));  // open: dp
  BCD_7S bcd_7s_9 (
    .Data(Periph_listener_1_address_001_value_7to4), .C(bcd_7s_9_c), .E(bcd_7s_9_e), .G(bcd_7s_9_g),
    .A(bcd_7s_9_a), .D(bcd_7s_9_d), .F(bcd_7s_9_f), .B(bcd_7s_9_b));
  RAM #(.addrWidth(12), .dataWidth(12), .trigger("high")) Memoire_instructions (
    .addr(Microprocesseur_1_address_to_mem_instr), .dout(Memoire_instructions_dout));  // open: we, oe, din
  RAM #(.addrWidth(12), .dataWidth(12), .trigger("falling")) Memoire_des_donnees (
    .addr(Memory_controller_1_address_to_mem_data), .we(Memory_controller_1_sd_to_mem_data),
    .oe(Memory_controller_1_ld_to_mem_data), .clk(Memory_controller_1_clk_to_mem_data),
    .din(Memory_controller_1_data_to_mem_data), .dout(Memoire_des_donnees_dout));
  _7_Segment_Display u_7_segment_display_11 (
    .g(bcd_7s_11_g), .f(bcd_7s_11_f), .a(bcd_7s_11_a), .b(bcd_7s_11_b), .e(bcd_7s_11_e), .d(bcd_7s_11_d),
    .c(bcd_7s_11_c));  // open: dp
  BCD_7S bcd_7s_10 (
    .Data(Periph_listener_1_address_001_value_3to0), .C(bcd_7s_10_c), .E(bcd_7s_10_e), .G(bcd_7s_10_g),
    .A(bcd_7s_10_a), .D(bcd_7s_10_d), .F(bcd_7s_10_f), .B(bcd_7s_10_b));
  _7_Segment_Display u_7_segment_display_12 (
    .g(bcd_7s_12_g), .f(bcd_7s_12_f), .a(bcd_7s_12_a), .b(bcd_7s_12_b), .e(bcd_7s_12_e), .d(bcd_7s_12_d),
    .c(bcd_7s_12_c));  // open: dp
  BCD_7S bcd_7s_11 (
    .Data(Periph_listener_1_address_000_value_bto8), .C(bcd_7s_11_c), .E(bcd_7s_11_e), .G(bcd_7s_11_g),
    .A(bcd_7s_11_a), .D(bcd_7s_11_d), .F(bcd_7s_11_f), .B(bcd_7s_11_b));
  BCD_7S bcd_7s_12 (
    .Data(Periph_listener_1_address_000_value_7to4), .C(bcd_7s_12_c), .E(bcd_7s_12_e), .G(bcd_7s_12_g),
    .A(bcd_7s_12_a), .D(bcd_7s_12_d), .F(bcd_7s_12_f), .B(bcd_7s_12_b));
  _7_Segment_Display u_7_segment_display_13 (
    .g(bcd_7s_13_g), .f(bcd_7s_13_f), .a(bcd_7s_13_a), .b(bcd_7s_13_b), .e(bcd_7s_13_e), .d(bcd_7s_13_d),
    .c(bcd_7s_13_c));  // open: dp
  BCD_7S bcd_7s_13 (
    .Data(Periph_listener_1_address_000_value_3to0), .C(bcd_7s_13_c), .E(bcd_7s_13_e), .G(bcd_7s_13_g),
    .A(bcd_7s_13_a), .D(bcd_7s_13_d), .F(bcd_7s_13_f), .B(bcd_7s_13_b));
  Periph_listener Periph_listener_1 (
    .Clk(Horloge_1_clk_out), .Data(Microprocesseur_1_sd_data_to_cache),
    .Address(Microprocesseur_1_address_to_cache), .En(Microprocesseur_1_sd_to_cache),
    .address_000_value_3to0(Periph_listener_1_address_000_value_3to0),
    .address_000_value_7to4(Periph_listener_1_address_000_value_7to4),
    .address_000_value_Bto8(Periph_listener_1_address_000_value_bto8),
    .address_001_value_3to0(Periph_listener_1_address_001_value_3to0),
    .address_001_value_7to4(Periph_listener_1_address_001_value_7to4),
    .address_001_value_Bto8(Periph_listener_1_address_001_value_bto8),
    .address_002_value_3to0(Periph_listener_1_address_002_value_3to0),
    .address_002_value_7to4(Periph_listener_1_address_002_value_7to4),
    .address_002_value_Bto8(Periph_listener_1_address_002_value_bto8));
  Memory_controller Memory_controller_1 (
    .ld_data_from_mem_data(Memoire_des_donnees_dout), .sd_data_from_cache(cache_1_sd_data_to_mem_contrl),
    .ld_from_cache(cache_1_ld_to_mem_contrl), .sd_from_cache(cache_1_sd_to_mem_contrl),
    .Clk(Horloge_1_clk_out), .Address_from_cache(cache_1_address_to_mem_contrl),
    .data_to_mem_data(Memory_controller_1_data_to_mem_data),
    .ld_to_mem_data(Memory_controller_1_ld_to_mem_data), .sd_to_mem_data(Memory_controller_1_sd_to_mem_data),
    .Ready_to_cache(Memory_controller_1_ready_to_cache),
    .ld_data_to_cache(Memory_controller_1_ld_data_to_cache),
    .Clk_to_mem_data(Memory_controller_1_clk_to_mem_data),
    .Address_to_mem_data(Memory_controller_1_address_to_mem_data));
endmodule

module Microprocesseur (
  input  Clk,
  input  [11:0] data_from_mem_instr,
  input  [11:0] ld_data_from_cache,
  input  ready_from_cache,
  output [11:0] sd_data_to_cache,
  output [11:0] address_to_mem_instr,
  output [11:0] address_to_cache,
  output ld_to_cache,
  output sd_to_cache
);

  wire and_1_out, branch_unit_1_is_instr_branch, branch_unit_1_is_taken_branch, hazard_detect_1_hazard,
       multiplexer_9_out, multiplexer_10_out, multiplexer_11_out, nand_1_out, not_1_out, or_1_out, or_2_out,
       xnor_1_out;
  wire [1:0] decode_1_pin_3to2, decode_1_pin_5to4, decode_1_pin_7to6, decode_3_pin_1to0, decode_3_pin_7to6,
       forwarding_unitv2_1_a, forwarding_unitv2_1_b, ID_EX_1_forwarda_out, ID_EX_1_forwardb_out,
       multiplexer_2_out, multiplexer_4_out;
  wire [3:0] decode_1_pin_bto8, decode_2_pin_bto8, decode_3_pin_bto8;
  wire [11:0] adder_1_out, ALU_1_result, branch_unit_1_npc, branch_unit_1_result, EX_MEM_1_ir_out,
       ID_EX_1_a_out, ID_EX_1_b_out, ID_EX_1_ir_out, ID_EX_1_npc_out, IF_ID_1_ir_out, IF_ID_1_npc_out,
       MEM_WB_1_ir_out, MEM_WB_1_load_out, MEM_WB_1_result_out, multiplexer_1_out, multiplexer_3_out,
       multiplexer_5_out, multiplexer_6_out, multiplexer_7_out, multiplexer_8_out, Registers_1_a,
       Registers_1_b;

  not not_1 (not_1_out, branch_unit_1_is_taken_branch);
  nand nand_1 (nand_1_out, hazard_detect_1_hazard, not_1_out);
  and and_1 (and_1_out, nand_1_out, xnor_1_out);
  Register #(.trigger("falling"), .width(12)) PC (
    .D(multiplexer_1_out), .en(and_1_out), .clk(Clk), .Q(address_to_mem_instr));  // open: clr
  // Probe on branch_unit_1_npc
  Adder #(.width(12)) adder_1 (.a(12'h1), .b(address_to_mem_instr), .out(adder_1_out));  // open: cin, cout
  Multiplexer #(.width(12)) multiplexer_1 (
    .in0(adder_1_out), .in1(branch_unit_1_npc), .out(multiplexer_1_out), .sel(branch_unit_1_is_taken_branch));
  // Probe on multiplexer_1_out
  IF_ID IF_ID_1 (
    .En(xnor_1_out), .NPC_in(multiplexer_1_out), .IR_in(data_from_mem_instr), .Clk(Clk),
    .NPC_out(IF_ID_1_npc_out), .IR_out(IF_ID_1_ir_out));
  // Probe on IF_ID_1_ir_out
  decode decode_1 (
    .Instruction(IF_ID_1_ir_out), .PIN_Bto8(decode_1_pin_bto8), .PIN_7to6(decode_1_pin_7to6),
    .PIN_5to4(decode_1_pin_5to4), .PIN_3to2(decode_1_pin_3to2));  // open: PIN_5to0, PIN_3to0, PIN_1to0
  Multiplexer #(.select(4), .width(2)) multiplexer_2 (
    .in0(decode_1_pin_5to4), .in1(decode_1_pin_5to4), .in2(decode_1_pin_5to4), .in3(decode_1_pin_5to4),
    .in4(decode_1_pin_5to4), .in5(decode_1_pin_5to4), .in6(decode_1_pin_5to4), .in7(decode_1_pin_5to4),
    .in8(decode_1_pin_5to4), .in9(decode_1_pin_5to4), .in10(decode_1_pin_5to4), .in11(decode_1_pin_5to4),
    .in12(decode_1_pin_5to4), .in13(decode_1_pin_5to4), .in14(decode_1_pin_7to6), .in15(decode_1_pin_7to6),
    .out(multiplexer_2_out), .sel(decode_1_pin_bto8));
  Hazard_Detect hazard_detect_1 (
    .ID_IR(IF_ID_1_ir_out), .EX_IR(ID_EX_1_ir_out), .MEM_IR(EX_MEM_1_ir_out), .Hazard(hazard_detect_1_hazard));
  or or_1 (or_1_out, hazard_detect_1_hazard, branch_unit_1_is_taken_branch);
  Multiplexer #(.width(12)) multiplexer_3 (
    .in0(IF_ID_1_ir_out), .in1({12{1'b0}}), .out(multiplexer_3_out), .sel(or_1_out));
  Multiplexer #(.select(4), .width(2)) multiplexer_4 (
    .in0(decode_1_pin_3to2), .in1(decode_1_pin_3to2), .in2(decode_1_pin_3to2), .in3(decode_1_pin_3to2),
    .in4(decode_1_pin_3to2), .in5(decode_1_pin_3to2), .in6(decode_1_pin_3to2), .in7(decode_1_pin_3to2),
    .in8(decode_1_pin_3to2), .in9(decode_1_pin_3to2), .in10(decode_1_pin_3to2), .in11(decode_1_pin_7to6),
    .in12(decode_1_pin_3to2), .in13(decode_1_pin_3to2), .in14(decode_1_pin_3to2), .in15(decode_1_pin_3to2),
    .out(multiplexer_4_out), .sel(decode_1_pin_bto8));
  Registers Registers_1 (
    .rs1(multiplexer_2_out), .rs2(multiplexer_4_out), .rd(decode_3_pin_7to6), .Write_en(multiplexer_11_out),
    .Data(multiplexer_8_out), .Clk(Clk), .A(Registers_1_a), .B(Registers_1_b));
  // Probe on ID_EX_1_ir_out
  ID_EX ID_EX_1 (
    .A_in(Registers_1_a), .B_in(Registers_1_b), .Clk(Clk), .NPC_in(IF_ID_1_npc_out),
    .IR_in(multiplexer_3_out), .En(xnor_1_out), .ForwardA_in(forwarding_unitv2_1_a),
    .ForwardB_in(forwarding_unitv2_1_b), .A_out(ID_EX_1_a_out), .B_out(ID_EX_1_b_out),
    .NPC_out(ID_EX_1_npc_out), .IR_out(ID_EX_1_ir_out), .ForwardA_out(ID_EX_1_forwarda_out),
    .ForwardB_out(ID_EX_1_forwardb_out));
  Multiplexer #(.select(2), .width(12)) multiplexer_5 (
    .in0(ID_EX_1_b_out), .in1(address_to_cache), .in2(MEM_WB_1_result_out), .in3(MEM_WB_1_load_out),
    .out(multiplexer_5_out), .sel(ID_EX_1_forwardb_out));
  Multiplexer #(.select(2), .width(12)) multiplexer_6 (
    .in0(ID_EX_1_a_out), .in1(address_to_cache), .in2(MEM_WB_1_result_out), .in3(MEM_WB_1_load_out),
    .out(multiplexer_6_out), .sel(ID_EX_1_forwarda_out));
  // Probe on multiplexer_5_out
  Branch_unit branch_unit_1 (
    .IR(ID_EX_1_ir_out), .NPC_in(ID_EX_1_npc_out), .A(multiplexer_6_out),
    .is_instr_branch(branch_unit_1_is_instr_branch), .is_taken_branch(branch_unit_1_is_taken_branch),
    .Result(branch_unit_1_result), .NPC(branch_unit_1_npc));
  ALU ALU_1 (.Instruction(ID_EX_1_ir_out), .A(multiplexer_6_out), .B(multiplexer_5_out), .Result(ALU_1_result));
  // Probe on multiplexer_7_out
  Multiplexer #(.width(12)) multiplexer_7 (
    .in0(ALU_1_result), .in1(branch_unit_1_result), .out(multiplexer_7_out),
    .sel(branch_unit_1_is_instr_branch));
  EX_MEM EX_MEM_1 (
    .Result_in(multiplexer_7_out), .B_in(multiplexer_5_out), .IR_in(ID_EX_1_ir_out), .En(xnor_1_out),
    .Clk(Clk), .IR_out(EX_MEM_1_ir_out), .Result_out(address_to_cache), .B_out(sd_data_to_cache));  // open: Branch_Taken_in, NPC_in, NPC_out, Branch_Taken_out
  Demultiplexer #(.select(4)) demultiplexer_1 (
    .out10(ld_to_cache), .out11(sd_to_cache), .in(1'b1), .sel(decode_2_pin_bto8));  // open: out0, out1, out2, out3, out4, out5, out6, out7, out8, out9, out12, out13, out14, out15
  decode decode_2 (
    .Instruction(EX_MEM_1_ir_out), .PIN_Bto8(decode_2_pin_bto8));  // open: PIN_7to6, PIN_5to4, PIN_5to0, PIN_3to2, PIN_3to0, PIN_1to0
  // Probe on EX_MEM_1_ir_out
  or or_2 (or_2_out, ld_to_cache, sd_to_cache);
  xnor xnor_1 (xnor_1_out, ready_from_cache, or_2_out);
  MEM_WB MEM_WB_1 (
    .Load_in(ld_data_from_cache), .Clk(Clk), .En(xnor_1_out), .IR_in(EX_MEM_1_ir_out),
    .Result_in(address_to_cache), .IR_out(MEM_WB_1_ir_out), .Result_out(MEM_WB_1_result_out),
    .Load_out(MEM_WB_1_load_out));
  decode decode_3 (
    .Instruction(MEM_WB_1_ir_out), .PIN_Bto8(decode_3_pin_bto8), .PIN_7to6(decode_3_pin_7to6),
    .PIN_1to0(decode_3_pin_1to0));  // open: PIN_5to4, PIN_5to0, PIN_3to2, PIN_3to0
  Multiplexer #(.select(4), .width(12)) multiplexer_8 (
    .in0(MEM_WB_1_result_out), .in1(MEM_WB_1_result_out), .in2(MEM_WB_1_result_out),
    .in3(MEM_WB_1_result_out), .in4(MEM_WB_1_result_out), .in5(MEM_WB_1_result_out),
    .in6(MEM_WB_1_result_out), .in7(MEM_WB_1_result_out), .in8(MEM_WB_1_result_out),
    .in9(MEM_WB_1_result_out), .in10(MEM_WB_1_load_out), .in11(MEM_WB_1_result_out),
    .in12(MEM_WB_1_result_out), .in13(MEM_WB_1_result_out), .out(multiplexer_8_out), .sel(decode_3_pin_bto8));  // open: in14, in15
  Multiplexer #(.select(2)) multiplexer_9 (
    .in0(1'b0), .in1(1'b1), .in2(1'b1), .in3(1'b1), .out(multiplexer_9_out), .sel(decode_3_pin_1to0));
  Multiplexer #(.select(2)) multiplexer_10 (
    .in0(1'b1), .in1(1'b0), .in2(1'b0), .in3(1'b1), .out(multiplexer_10_out), .sel(decode_3_pin_1to0));
  Forwarding_unitV2 forwarding_unitv2_1 (
    .EX_IR(ID_EX_1_ir_out), .MEM_IR(EX_MEM_1_ir_out), .WB_IR(MEM_WB_1_ir_out), .A(forwarding_unitv2_1_a),
    .B(forwarding_unitv2_1_b));
  Multiplexer #(.select(4)) multiplexer_11 (
    .in0(multiplexer_9_out), .in1(1'b1), .in2(multiplexer_10_out), .in3(1'b1), .in4(1'b1), .in5(1'b1),
    .in6(1'b1), .in7(1'b1), .in8(1'b1), .in9(1'b1), .in10(1'b1), .in11(1'b0), .in12(1'b1), .in13(1'b1),
    .in14(1'b0), .in15(1'b0), .out(multiplexer_11_out), .sel(decode_3_pin_bto8));
endmodule

module IF_ID (
  input  Clk,
  input  En,
  input  [11:0] NPC_in,
  input  [11:0] IR_in,
  output [11:0] NPC_out,
  output [11:0] IR_out
);

  Register #(.width(12)) NPC_reg12 (.D(NPC_in), .en(En), .clk(Clk), .Q(NPC_out));  // open: clr
  Register #(.width(12)) IR_reg12 (.D(IR_in), .en(En), .clk(Clk), .Q(IR_out));  // open: clr
endmodule

module ID_EX (
  input  Clk,
  input  En,
  input  [11:0] A_in,
  input  [11:0] B_in,
  input  [11:0] NPC_in,
  input  [11:0] IR_in,
  input  [1:0] ForwardA_in,
  input  [1:0] ForwardB_in,
  output [11:0] A_out,
  output [11:0] B_out,
  output [11:0] NPC_out,
  output [11:0] IR_out,
  output [1:0] ForwardA_out,
  output [1:0] ForwardB_out
);

  Register #(.width(12)) A_reg12 (.D(A_in), .en(En), .clk(Clk), .Q(A_out));  // open: clr
  Register #(.width(12)) B_reg12 (.D(B_in), .en(En), .clk(Clk), .Q(B_out));  // open: clr
  Register #(.width(12)) NPC_reg12 (.D(NPC_in), .en(En), .clk(Clk), .Q(NPC_out));  // open: clr
  Register #(.width(12)) IR_reg12 (.D(IR_in), .en(En), .clk(Clk), .Q(IR_out));  // open: clr
  Register #(.width(2)) ForwardA_reg12 (.D(ForwardA_in), .en(En), .clk(Clk), .Q(ForwardA_out));  // open: clr
  Register #(.width(2)) ForwardB_reg12 (.D(ForwardB_in), .en(En), .clk(Clk), .Q(ForwardB_out));  // open: clr
endmodule

module EX_MEM (
  input  Clk,
  input  En,
  input  [11:0] NPC_in,
  input  [11:0] IR_in,
  input  Branch_Taken_in,
  input  [11:0] Result_in,
  input  [11:0] B_in,
  output [11:0] NPC_out,
  output [11:0] IR_out,
  output Branch_Taken_out,
  output [11:0] Result_out,
  output [11:0] B_out
);

  Register #(.width(12)) NPC_reg12 (.D(NPC_in), .en(En), .clk(Clk), .Q(NPC_out));  // open: clr
  Register #(.width(12)) IR_reg12 (.D(IR_in), .en(En), .clk(Clk), .Q(IR_out));  // open: clr
  Register #(.width(1)) Branch_reg1 (.D(Branch_Taken_in), .en(En), .clk(Clk), .Q(Branch_Taken_out));  // open: clr
  Register #(.width(12)) Result_reg12 (.D(Result_in), .en(En), .clk(Clk), .Q(Result_out));  // open: clr
  Register #(.width(12)) B_reg12 (.D(B_in), .en(En), .clk(Clk), .Q(B_out));  // open: clr
endmodule

module MEM_WB (
  input  Clk,
  input  En,
  input  [11:0] IR_in,
  input  [11:0] Result_in,
  input  [11:0] Load_in,
  output [11:0] IR_out,
  output [11:0] Result_out,
  output [11:0] Load_out
);

  wire and_1_out, comparator_1_eq, not_1_out;

  Register #(.width(12)) IR_reg12 (.D(IR_in), .en(En), .clk(Clk), .Q(IR_out));  // open: clr
  Register #(.width(12)) Result_reg12 (.D(Result_in), .en(not_1_out), .clk(Clk), .Q(Result_out));  // open: clr
  Register #(.width(12)) Load_reg12 (.D(Load_in), .en(not_1_out), .clk(Clk), .Q(Load_out));  // open: clr
  Comparator #(.width(12)) comparator_1 (.a(IR_in), .b({12{1'b0}}), .eq(comparator_1_eq));  // open: gt, lt
  and and_1 (and_1_out, comparator_1_eq, En);
  not not_1 (not_1_out, and_1_out);
endmodule

module ALU (
  input  [11:0] Instruction,
  input  [11:0] A,
  input  [11:0] B,
  output [11:0] Result
);

  wire [1:0] decode_1_pin_1to0;
  wire [3:0] decode_1_pin_3to0, decode_1_pin_bto8;
  wire [11:0] adder_1_out, adder_2_out, and_1_out, divider_1_out, divider_1_rem, divider_2_out,
       divider_2_rem, multiplexer_1_out, multiplexer_2_out, multiplexer_3_out, multiplier_1_out,
       multiplier_2_out, not_1_out, or_1_out, shifter_1_out, shifter_2_out, subtractor_1_out,
       subtractor_2_out, xor_1_out;

  decode decode_1 (
    .Instruction(Instruction), .PIN_Bto8(decode_1_pin_bto8), .PIN_3to0(decode_1_pin_3to0),
    .PIN_1to0(decode_1_pin_1to0));  // open: PIN_7to6, PIN_5to4, PIN_5to0, PIN_3to2
  Adder #(.width(12)) adder_1 (.a(A), .b(B), .out(adder_1_out));  // open: cin, cout
  Subtractor #(.width(12)) subtractor_1 (.a(A), .b(B), .out(subtractor_1_out));  // open: bin, bout
  Multiplier #(.width(12)) multiplier_1 (.a(A), .b(B), .out(multiplier_1_out));  // open: cin, cout
  Divider #(.width(12)) divider_1 (.a(A), .b(B), .out(divider_1_out), .rem(divider_1_rem));  // open: upper
  assign and_1_out = A & B;  // AND_Gate and_1, 12 bits wide
  assign or_1_out = A | B;  // OR_Gate or_1, 12 bits wide
  assign xor_1_out = A ^ B;  // XOR_Gate xor_1, 12 bits wide
  assign not_1_out = ~A;  // NOT_Gate not_1, 12 bits wide
  Adder #(.width(12)) adder_2 (.a(A), .b({{8{1'b0}}, decode_1_pin_3to0}), .out(adder_2_out));  // open: cin, cout
  Subtractor #(.width(12)) subtractor_2 (
    .a(A), .b({{8{1'b0}}, decode_1_pin_3to0}), .out(subtractor_2_out));  // open: bin, bout
  Multiplier #(.width(12)) multiplier_2 (
    .a(A), .b({{8{1'b0}}, decode_1_pin_3to0}), .out(multiplier_2_out));  // open: cin, cout
  Divider #(.width(12)) divider_2 (
    .a(A), .b({{8{1'b0}}, decode_1_pin_3to0}), .out(divider_2_out), .rem(divider_2_rem));  // open: upper
  Shifter #(.width(12)) shifter_1 (.in(A), .\dist (decode_1_pin_3to0), .out(shifter_1_out));
  Shifter #(.shift("lr"), .width(12)) shifter_2 (.in(A), .\dist (decode_1_pin_3to0), .out(shifter_2_out));
  Multiplexer #(.enable("true"), .select(2), .width(12)) multiplexer_1 (
    .in0({12{1'b0}}), .in1(adder_1_out), .in2(subtractor_1_out), .in3(multiplier_1_out),
    .out(multiplexer_1_out), .sel(decode_1_pin_1to0));  // open: en
  Multiplexer #(.enable("true"), .select(2), .width(12)) multiplexer_2 (
    .in0(divider_1_out), .in1(divider_1_rem), .in2(and_1_out), .in3(or_1_out), .out(multiplexer_2_out),
    .sel(decode_1_pin_1to0));  // open: en
  Multiplexer #(.enable("true"), .select(2), .width(12)) multiplexer_3 (
    .in0(xor_1_out), .in1({12{1'b0}}), .in2({12{1'b0}}), .in3(not_1_out), .out(multiplexer_3_out),
    .sel(decode_1_pin_1to0));  // open: en
  Multiplexer #(.enable("true"), .select(4), .width(12)) multiplexer_4 (
    .in0(multiplexer_1_out), .in1(multiplexer_2_out), .in2(multiplexer_3_out), .in3(adder_2_out),
    .in4(subtractor_2_out), .in5(multiplier_2_out), .in6(divider_2_out), .in7(divider_2_rem),
    .in8(shifter_1_out), .in9(shifter_2_out), .in10(adder_2_out), .in11(adder_2_out), .in12({12{1'b0}}),
    .in13({12{1'b0}}), .in14({12{1'b0}}), .in15({12{1'b0}}), .out(Result), .sel(decode_1_pin_bto8));  // open: en
endmodule

module Registers (
  input  Clk,
  input  [1:0] rs1,
  input  [1:0] rs2,
  input  [1:0] rd,
  input  Write_en,
  input  [11:0] Data,
  output [11:0] A,
  output [11:0] B
);

  wire demultiplexer_1_out0, demultiplexer_1_out1, demultiplexer_1_out2, demultiplexer_1_out3;
  wire [11:0] demultiplexer_2_out0, demultiplexer_2_out1, demultiplexer_2_out2, demultiplexer_2_out3, reg0_q,
       reg1_q, reg2_q, reg3_q;

  Demultiplexer #(.enable("true"), .select(2)) demultiplexer_1 (
    .out0(demultiplexer_1_out0), .out1(demultiplexer_1_out1), .out2(demultiplexer_1_out2),
    .out3(demultiplexer_1_out3), .in(Write_en), .sel(rd));  // open: en
  Demultiplexer #(.enable("true"), .select(2), .width(12)) demultiplexer_2 (
    .out0(demultiplexer_2_out0), .out1(demultiplexer_2_out1), .out2(demultiplexer_2_out2),
    .out3(demultiplexer_2_out3), .in(Data), .sel(rd));  // open: en
  Register #(.trigger("falling"), .width(12)) reg0 (
    .D(demultiplexer_2_out0), .en(demultiplexer_1_out0), .clk(Clk), .Q(reg0_q));  // open: clr
  Register #(.trigger("falling"), .width(12)) reg1 (
    .D(demultiplexer_2_out1), .en(demultiplexer_1_out1), .clk(Clk), .Q(reg1_q));  // open: clr
  Register #(.trigger("falling"), .width(12)) reg2 (
    .D(demultiplexer_2_out2), .en(demultiplexer_1_out2), .clk(Clk), .Q(reg2_q));  // open: clr
  Register #(.trigger("falling"), .width(12)) reg3 (
    .D(demultiplexer_2_out3), .en(demultiplexer_1_out3), .clk(Clk), .Q(reg3_q));  // open: clr
  Multiplexer #(.enable("true"), .select(2), .width(12)) multiplexer_1 (
    .in0(reg0_q), .in1(reg1_q), .in2(reg2_q), .in3(reg3_q), .out(A), .sel(rs1));  // open: en
  Multiplexer #(.enable("true"), .select(2), .width(12)) multiplexer_2 (
    .in0(reg0_q), .in1(reg1_q), .in2(reg2_q), .in3(reg3_q), .out(B), .sel(rs2));  // open: en
endmodule

module Branch_unit (
  input  [11:0] IR,
  input  [11:0] NPC_in,
  input  [11:0] A,
  output is_instr_branch,
  output is_taken_branch,
  output [11:0] Result,
  output [11:0] NPC
);

  wire comparator_1_eq, multiplexer_9_out, multiplexer_10_out, multiplexer_11_out, multiplexer_13_out,
       multiplexer_14_out, multiplexer_15_out, not_1_out;
  wire [1:0] decode_1_pin_1to0;
  wire [3:0] decode_1_pin_3to0, decode_1_pin_bto8;
  wire [5:0] decode_1_pin_5to0;
  wire [11:0] adder_1_out, adder_2_out, multiplexer_1_out, multiplexer_2_out, multiplexer_3_out,
       multiplexer_5_out, multiplexer_6_out, multiplexer_7_out, subtractor_1_out;

  decode decode_1 (
    .Instruction(IR), .PIN_Bto8(decode_1_pin_bto8), .PIN_5to0(decode_1_pin_5to0),
    .PIN_3to0(decode_1_pin_3to0), .PIN_1to0(decode_1_pin_1to0));  // open: PIN_7to6, PIN_5to4, PIN_3to2
  Adder #(.width(12)) adder_1 (
    .a({{7{decode_1_pin_5to0[5]}}, decode_1_pin_5to0[4:0]}), .b(NPC_in), .out(adder_1_out));  // open: cin, cout
  Subtractor #(.width(12)) subtractor_1 (.a(adder_1_out), .b(12'h1), .out(subtractor_1_out));  // open: bin, bout
  Adder #(.width(12)) adder_2 (.a({{8{1'b0}}, decode_1_pin_3to0}), .b(A), .out(adder_2_out));  // open: cin, cout
  Multiplexer #(.enable("true"), .select(2), .width(12)) multiplexer_1 (
    .in0(NPC_in), .in1(NPC_in), .in2(NPC_in), .in3(NPC_in), .out(multiplexer_1_out), .sel(decode_1_pin_1to0));  // open: en
  Multiplexer #(.enable("true"), .select(2), .width(12)) multiplexer_2 (
    .in0(NPC_in), .in1(NPC_in), .in2(NPC_in), .in3(NPC_in), .out(multiplexer_2_out), .sel(decode_1_pin_1to0));  // open: en
  Multiplexer #(.enable("true"), .select(2), .width(12)) multiplexer_3 (
    .in0(NPC_in), .in1(NPC_in), .in2(NPC_in), .in3(NPC_in), .out(multiplexer_3_out), .sel(decode_1_pin_1to0));  // open: en
  Multiplexer #(.enable("true"), .select(4), .width(12)) multiplexer_4 (
    .in0(multiplexer_1_out), .in1(multiplexer_2_out), .in2(multiplexer_3_out), .in3(NPC_in), .in4(NPC_in),
    .in5(NPC_in), .in6(NPC_in), .in7(NPC_in), .in8(NPC_in), .in9(NPC_in), .in10(NPC_in), .in11(NPC_in),
    .in12(adder_2_out), .in13(subtractor_1_out), .in14(subtractor_1_out), .in15(subtractor_1_out), .out(NPC),
    .sel(decode_1_pin_bto8));  // open: en
  Comparator #(.width(12)) comparator_1 (.a({12{1'b0}}), .b(A), .eq(comparator_1_eq));  // open: gt, lt
  Multiplexer #(.enable("true"), .select(2), .width(12)) multiplexer_5 (
    .in0({12{1'b0}}), .in1({12{1'b0}}), .in2({12{1'b0}}), .in3({12{1'b0}}), .out(multiplexer_5_out),
    .sel(decode_1_pin_1to0));  // open: en
  Multiplexer #(.enable("true"), .select(2), .width(12)) multiplexer_6 (
    .in0({12{1'b0}}), .in1({12{1'b0}}), .in2({12{1'b0}}), .in3({12{1'b0}}), .out(multiplexer_6_out),
    .sel(decode_1_pin_1to0));  // open: en
  Multiplexer #(.enable("true"), .select(2), .width(12)) multiplexer_7 (
    .in0({12{1'b0}}), .in1({12{1'b0}}), .in2({12{1'b0}}), .in3({12{1'b0}}), .out(multiplexer_7_out),
    .sel(decode_1_pin_1to0));  // open: en
  not not_1 (not_1_out, comparator_1_eq);
  Multiplexer #(.enable("true"), .select(4), .width(12)) multiplexer_8 (
    .in0(multiplexer_5_out), .in1(multiplexer_6_out), .in2(multiplexer_7_out), .in3({12{1'b0}}),
    .in4({12{1'b0}}), .in5({12{1'b0}}), .in6({12{1'b0}}), .in7({12{1'b0}}), .in8({12{1'b0}}),
    .in9({12{1'b0}}), .in10({12{1'b0}}), .in11({12{1'b0}}), .in12(NPC_in), .in13(NPC_in), .in14({12{1'b0}}),
    .in15({12{1'b0}}), .out(Result), .sel(decode_1_pin_bto8));  // open: en
  Multiplexer #(.enable("true"), .select(2)) multiplexer_9 (
    .in0(1'b0), .in1(1'b0), .in2(1'b0), .in3(1'b0), .out(multiplexer_9_out), .sel(decode_1_pin_1to0));  // open: en
  Multiplexer #(.enable("true"), .select(2)) multiplexer_10 (
    .in0(1'b0), .in1(1'b0), .in2(1'b0), .in3(1'b0), .out(multiplexer_10_out), .sel(decode_1_pin_1to0));  // open: en
  Multiplexer #(.enable("true"), .select(2)) multiplexer_11 (
    .in0(1'b0), .in1(1'b0), .in2(1'b0), .in3(1'b0), .out(multiplexer_11_out), .sel(decode_1_pin_1to0));  // open: en
  Multiplexer #(.enable("true"), .select(4)) multiplexer_12 (
    .in0(multiplexer_9_out), .in1(multiplexer_10_out), .in2(multiplexer_11_out), .in3(1'b0), .in4(1'b0),
    .in5(1'b0), .in6(1'b0), .in7(1'b0), .in8(1'b0), .in9(1'b0), .in10(1'b0), .in11(1'b0), .in12(1'b1),
    .in13(1'b1), .in14(comparator_1_eq), .in15(not_1_out), .out(is_taken_branch), .sel(decode_1_pin_bto8));  // open: en
  Multiplexer #(.enable("true"), .select(2)) multiplexer_13 (
    .in0(1'b0), .in1(1'b0), .in2(1'b0), .in3(1'b0), .out(multiplexer_13_out), .sel(decode_1_pin_1to0));  // open: en
  Multiplexer #(.enable("true"), .select(2)) multiplexer_14 (
    .in0(1'b0), .in1(1'b0), .in2(1'b0), .in3(1'b0), .out(multiplexer_14_out), .sel(decode_1_pin_1to0));  // open: en
  Multiplexer #(.enable("true"), .select(2)) multiplexer_15 (
    .in0(1'b0), .in1(1'b0), .in2(1'b0), .in3(1'b0), .out(multiplexer_15_out), .sel(decode_1_pin_1to0));  // open: en
  Multiplexer #(.enable("true"), .select(4)) multiplexer_16 (
    .in0(multiplexer_13_out), .in1(multiplexer_14_out), .in2(multiplexer_15_out), .in3(1'b0), .in4(1'b0),
    .in5(1'b0), .in6(1'b0), .in7(1'b0), .in8(1'b0), .in9(1'b0), .in10(1'b0), .in11(1'b0), .in12(1'b1),
    .in13(1'b1), .in14(1'b1), .in15(1'b1), .out(is_instr_branch), .sel(decode_1_pin_bto8));  // open: en
endmodule

module decode (
  input  [11:0] Instruction,
  output [3:0] PIN_Bto8,
  output [1:0] PIN_7to6,
  output [1:0] PIN_5to4,
  output [5:0] PIN_5to0,
  output [1:0] PIN_3to2,
  output [3:0] PIN_3to0,
  output [1:0] PIN_1to0
);


  assign PIN_1to0 = Instruction[1:0];
  assign PIN_3to0 = Instruction[3:0];
  assign PIN_3to2 = Instruction[3:2];
  assign PIN_5to0 = Instruction[5:0];
  assign PIN_5to4 = Instruction[5:4];
  assign PIN_7to6 = Instruction[7:6];
  assign PIN_Bto8 = Instruction[11:8];
endmodule

module Horloge (
  input  Clk_in,
  input  [11:0] Data,
  input  [11:0] Listen_address,
  input  En,
  output Clk_out,
  output [11:0] Count
);

  wire and_1_out, comparator_1_eq, comparator_2_eq, not_1_out, register_1_q;
  wire [11:0] adder_1_out;

  Comparator #(.width(12)) comparator_1 (.a(Data), .b(12'h458), .eq(comparator_1_eq));  // open: gt, lt
  Comparator #(.width(12)) comparator_2 (.a(Listen_address), .b({12{1'b1}}), .eq(comparator_2_eq));  // open: gt, lt
  and and_1 (and_1_out, comparator_1_eq, comparator_2_eq, En);
  Register #(.width(1)) register_1 (.D(and_1_out), .en(and_1_out), .clk(Clk_in), .Q(register_1_q));  // open: clr
  not not_1 (not_1_out, register_1_q);
  and and_2 (Clk_out, Clk_in, not_1_out);
  Register #(.width(12)) register_2 (.D(adder_1_out), .en(1'b1), .clk(Clk_out), .Q(Count));  // open: clr
  Adder #(.width(12)) adder_1 (.a(Count), .b(12'h1), .out(adder_1_out));  // open: cin, cout
endmodule

module BCD_7S (
  input  [3:0] Data,
  output A,
  output B,
  output C,
  output D,
  output E,
  output F,
  output G
);

  Multiplexer #(.enable("true"), .select(4), .width(7)) multiplexer_1 (
    .in0(7'b0111111), .in1(7'b0000110), .in2(7'b1011011), .in3(7'b1001111), .in4(7'b1100110),
    .in5(7'b1101101), .in6(7'b1111101), .in7(7'b0000111), .in8({7{1'b1}}), .in9(7'b1100111),
    .in10(7'b1110111), .in11(7'b1111100), .in12(7'b0111001), .in13(7'b1011110), .in14(7'b1111001),
    .in15(7'b1110001), .out({G, F, E, D, C, B, A}), .sel(Data));  // open: en
endmodule

module Periph_listener (
  input  Clk,
  input  [11:0] Data,
  input  [11:0] Address,
  input  En,
  output [3:0] address_000_value_3to0,
  output [3:0] address_000_value_7to4,
  output [3:0] address_000_value_Bto8,
  output [3:0] address_001_value_3to0,
  output [3:0] address_001_value_7to4,
  output [3:0] address_001_value_Bto8,
  output [3:0] address_002_value_3to0,
  output [3:0] address_002_value_7to4,
  output [3:0] address_002_value_Bto8
);

  wire and_1_out, and_2_out, and_3_out, comparator_1_eq, comparator_2_eq, comparator_3_eq;

  Comparator #(.width(12)) comparator_1 (.a(Address), .b({12{1'b0}}), .eq(comparator_1_eq));  // open: gt, lt
  Comparator #(.width(12)) comparator_2 (.a(Address), .b(12'h1), .eq(comparator_2_eq));  // open: gt, lt
  Comparator #(.width(12)) comparator_3 (.a(Address), .b(12'h2), .eq(comparator_3_eq));  // open: gt, lt
  Register #(.width(12)) register_1 (
    .D(Data), .en(and_1_out), .clk(Clk),
    .Q({address_000_value_Bto8, address_000_value_7to4, address_000_value_3to0}));  // open: clr
  and and_1 (and_1_out, comparator_1_eq, En);
  Register #(.width(12)) register_2 (
    .D(Data), .en(and_2_out), .clk(Clk),
    .Q({address_001_value_Bto8, address_001_value_7to4, address_001_value_3to0}));  // open: clr
  and and_2 (and_2_out, comparator_2_eq, En);
  Register #(.width(12)) register_3 (
    .D(Data), .en(and_3_out), .clk(Clk),
    .Q({address_002_value_Bto8, address_002_value_7to4, address_002_value_3to0}));  // open: clr
  and and_3 (and_3_out, comparator_3_eq, En);
endmodule

module Cache (
  input  Ready_from_mem_contrl,
  input  Clk,
  input  [11:0] Address_from_up,
  input  [11:0] ld_data_from_mem_contrl,
  input  [11:0] sd_data_from_up,
  input  ld_from_up,
  input  sd_from_up,
  output Ready_to_up,
  output [11:0] Address_to_mem_contrl,
  output [11:0] ld_data_to_up,
  output [11:0] sd_data_to_mem_contrl,
  output ld_to_mem_contrl,
  output sd_to_mem_contrl
);

  wire and_2_out, and_4_out, not_1_out, not_2_out, not_3_out, register_1_q, register_2_q;

  Memory_block B0 ();  // open: Clk, Data_in, Data_out
  Memory_block B1 ();  // open: Clk, Data_in, Data_out
  Memory_block B2 ();  // open: Clk, Data_in, Data_out
  Memory_block B3 ();  // open: Clk, Data_in, Data_out
  not not_1 (not_1_out, Ready_from_mem_contrl);
  Register #(.width(1)) register_1 (.D(and_2_out), .en(1'b1), .clk(Clk), .Q(register_1_q));  // open: clr
  Register #(.width(1)) register_2 (.D(and_4_out), .en(1'b1), .clk(Clk), .Q(register_2_q));  // open: clr
  not not_2 (not_2_out, register_1_q);
  not not_3 (not_3_out, register_2_q);
  and and_1 (ld_to_mem_contrl, not_2_out, ld_from_up);
  and and_2 (and_2_out, ld_from_up, not_1_out);
  and and_3 (sd_to_mem_contrl, not_3_out, sd_from_up);
  and and_4 (and_4_out, sd_from_up, not_1_out);

  assign Address_to_mem_contrl = Address_from_up;
  assign ld_data_to_up = ld_data_from_mem_contrl;
  assign Ready_to_up = Ready_from_mem_contrl;
  assign sd_data_to_mem_contrl = sd_data_from_up;
endmodule

module Memory_block (
  input  Clk,
  input  [11:0] Data_in,
  output [11:0] Data_out
);

  Register #(.width(12)) register_1 ();  // open: D, en, clk, Q, clr
  Register #(.width(12)) register_2 ();  // open: D, en, clk, Q, clr
endmodule

module Memory_controller (
  input  Clk,
  input  [11:0] Address_from_cache,
  input  [11:0] ld_data_from_mem_data,
  input  [11:0] sd_data_from_cache,
  input  ld_from_cache,
  input  sd_from_cache,
  output Clk_to_mem_data,
  output [11:0] Address_to_mem_data,
  output [11:0] data_to_mem_data,
  output ld_to_mem_data,
  output sd_to_mem_data,
  output Ready_to_cache,
  output [11:0] ld_data_to_cache
);

  wire [11:0] multiplexer_1_out;
  wire [24:24] register_8_q;
  wire [25:0] register_1_q, register_2_q, register_3_q, register_4_q, register_5_q, register_6_q,
       register_7_q;

  Multiplexer #(.enable("true"), .width(12)) multiplexer_1 (
    .in0(ld_data_from_mem_data), .in1(sd_data_from_cache), .out(multiplexer_1_out), .sel(sd_from_cache));  // open: en
  Register #(.width(26)) register_1 (
    .D({sd_from_cache, ld_from_cache, multiplexer_1_out, Address_from_cache}), .en(1'b1), .clk(Clk),
    .Q(register_1_q));  // open: clr
  Register #(.width(26)) register_2 (.D(register_1_q), .en(1'b1), .clk(Clk), .Q(register_2_q));  // open: clr
  Register #(.width(26)) register_3 (.D(register_2_q), .en(1'b1), .clk(Clk), .Q(register_3_q));  // open: clr
  Register #(.width(26)) register_4 (.D(register_3_q), .en(1'b1), .clk(Clk), .Q(register_4_q));  // open: clr
  Register #(.width(26)) register_5 (.D(register_4_q), .en(1'b1), .clk(Clk), .Q(register_5_q));  // open: clr
  Register #(.width(26)) register_6 (.D(register_5_q), .en(1'b1), .clk(Clk), .Q(register_6_q));  // open: clr
  Register #(.width(26)) register_7 (.D(register_6_q), .en(1'b1), .clk(Clk), .Q(register_7_q));  // open: clr
  Register #(.width(26)) register_8 (
    .D(register_7_q), .en(1'b1), .clk(Clk),
    .Q({sd_to_mem_data, register_8_q[24], data_to_mem_data, Address_to_mem_data}));  // open: clr
  or or_1 (Ready_to_cache, register_8_q[24], sd_to_mem_data);

  assign Clk_to_mem_data = Clk;
  assign ld_data_to_cache = ld_data_from_mem_data;
  assign ld_to_mem_data = 1'b1;
endmodule

module Hazard_Detect (
  input  [11:0] ID_IR,
  input  [11:0] EX_IR,
  input  [11:0] MEM_IR,
  output Hazard
);

  wire and_1_out, and_2_out, and_3_out, and_4_out, and_5_out, and_6_out, and_7_out, and_8_out,
       comparator_1_eq, comparator_2_eq, comparator_3_eq, comparator_4_eq, not_1_out, not_2_out, not_3_out,
       or_1_out, or_2_out, or_3_out, register_decode_1_is_nop, register_decode_1_is_rs2,
       register_decode_2_is_nop, register_decode_2_is_rd, register_decode_3_is_nop, register_decode_3_is_rd;
  wire [1:0] register_decode_1_rs1, register_decode_1_rs2, register_decode_2_rd, register_decode_3_rd;

  Register_decode register_decode_1 (
    .Instr(ID_IR), .Rs1(register_decode_1_rs1), .Rs2(register_decode_1_rs2),
    .is_nop(register_decode_1_is_nop), .is_rs2(register_decode_1_is_rs2));  // open: Rd, is_rd
  Register_decode register_decode_2 (
    .Instr(EX_IR), .Rd(register_decode_2_rd), .is_nop(register_decode_2_is_nop),
    .is_rd(register_decode_2_is_rd));  // open: Rs1, Rs2, is_rs2
  Register_decode register_decode_3 (
    .Instr(MEM_IR), .Rd(register_decode_3_rd), .is_nop(register_decode_3_is_nop),
    .is_rd(register_decode_3_is_rd));  // open: Rs1, Rs2, is_rs2
  Comparator #(.mode("unsigned"), .width(2)) comparator_1 (
    .a(register_decode_1_rs1), .b(register_decode_2_rd), .eq(comparator_1_eq));  // open: gt, lt
  Comparator #(.mode("unsigned"), .width(2)) comparator_2 (
    .a(register_decode_1_rs2), .b(register_decode_2_rd), .eq(comparator_2_eq));  // open: gt, lt
  Comparator #(.mode("unsigned"), .width(2)) comparator_3 (
    .a(register_decode_1_rs2), .b(register_decode_3_rd), .eq(comparator_3_eq));  // open: gt, lt
  Comparator #(.mode("unsigned"), .width(2)) comparator_4 (
    .a(register_decode_3_rd), .b(register_decode_1_rs1), .eq(comparator_4_eq));  // open: gt, lt
  and and_1 (and_1_out, comparator_1_eq, register_decode_2_is_rd);
  and and_2 (and_2_out, comparator_2_eq, register_decode_2_is_rd);
  and and_3 (and_3_out, comparator_3_eq, register_decode_3_is_rd);
  and and_4 (and_4_out, comparator_4_eq, register_decode_3_is_rd);
  and and_5 (and_5_out, register_decode_1_is_rs2, and_2_out);
  and and_6 (and_6_out, register_decode_1_is_rs2, and_3_out);
  or or_1 (or_1_out, and_1_out, and_5_out);
  or or_2 (or_2_out, and_6_out, and_4_out);
  not not_1 (not_1_out, register_decode_3_is_nop);
  and and_7 (and_7_out, or_1_out, not_2_out);
  not not_2 (not_2_out, register_decode_2_is_nop);
  and and_8 (and_8_out, not_1_out, or_2_out);
  not not_3 (not_3_out, register_decode_1_is_nop);
  and and_9 (Hazard, not_3_out, or_3_out);
  or or_3 (or_3_out, and_7_out, and_8_out);
endmodule

module Register_decode (
  input  [11:0] Instr,
  output [1:0] Rd,
  output [1:0] Rs1,
  output [1:0] Rs2,
  output is_nop,
  output is_rd,
  output is_rs2
);

  wire comparator_1_eq, comparator_2_eq, comparator_3_gt, comparator_4_gt, comparator_5_eq, comparator_6_eq,
       comparator_7_eq, nand_1_out, not_1_out, or_1_out;
  wire [1:0] decode_1_pin_1to0, decode_1_pin_3to2, decode_1_pin_5to4, decode_1_pin_7to6;
  wire [3:0] decode_1_pin_bto8;

  decode decode_1 (
    .Instruction(Instr), .PIN_Bto8(decode_1_pin_bto8), .PIN_7to6(decode_1_pin_7to6),
    .PIN_5to4(decode_1_pin_5to4), .PIN_3to2(decode_1_pin_3to2), .PIN_1to0(decode_1_pin_1to0));  // open: PIN_5to0, PIN_3to0
  Comparator #(.mode("unsigned"), .width(4)) comparator_1 (
    .a(decode_1_pin_bto8), .b(4'b0000), .eq(comparator_1_eq));  // open: gt, lt
  Comparator #(.mode("unsigned"), .width(2)) comparator_2 (
    .a(decode_1_pin_1to0), .b(2'b00), .eq(comparator_2_eq));  // open: gt, lt
  Comparator #(.mode("unsigned"), .width(4)) comparator_3 (
    .a(decode_1_pin_bto8), .b(4'b1101), .gt(comparator_3_gt));  // open: eq, lt
  Comparator #(.mode("unsigned"), .width(4)) comparator_4 (
    .a(decode_1_pin_bto8), .b(4'b0010), .gt(comparator_4_gt));  // open: eq, lt
  Comparator #(.mode("unsigned"), .width(4)) comparator_5 (
    .a(decode_1_pin_bto8), .b(4'b1011), .eq(comparator_5_eq));  // open: gt, lt
  Comparator #(.mode("unsigned"), .width(4)) comparator_6 (
    .a(decode_1_pin_bto8), .b(4'b0010), .eq(comparator_6_eq));  // open: gt, lt
  Comparator #(.mode("unsigned"), .width(2)) comparator_7 (
    .a(decode_1_pin_1to0), .b(2'b11), .eq(comparator_7_eq));  // open: gt, lt
  Multiplexer #(.select(4), .width(2)) multiplexer_1 (
    .in0(decode_1_pin_7to6), .in1(decode_1_pin_7to6), .in2(decode_1_pin_7to6), .in3(decode_1_pin_7to6),
    .in4(decode_1_pin_7to6), .in5(decode_1_pin_7to6), .in6(decode_1_pin_7to6), .in7(decode_1_pin_7to6),
    .in8(decode_1_pin_7to6), .in9(decode_1_pin_7to6), .in10(decode_1_pin_7to6), .in11(decode_1_pin_7to6),
    .in12(decode_1_pin_7to6), .in13(decode_1_pin_7to6), .in14(2'b00), .in15(2'b00), .out(Rd),
    .sel(decode_1_pin_bto8));
  Multiplexer #(.select(4), .width(2)) multiplexer_2 (
    .in0(decode_1_pin_5to4), .in1(decode_1_pin_5to4), .in2(decode_1_pin_5to4), .in3(decode_1_pin_5to4),
    .in4(decode_1_pin_5to4), .in5(decode_1_pin_5to4), .in6(decode_1_pin_5to4), .in7(decode_1_pin_5to4),
    .in8(decode_1_pin_5to4), .in9(decode_1_pin_5to4), .in10(decode_1_pin_5to4), .in11(decode_1_pin_7to6),
    .in12(decode_1_pin_5to4), .in13(2'b00), .in14(decode_1_pin_7to6), .in15(decode_1_pin_7to6), .out(Rs1),
    .sel(decode_1_pin_bto8));
  Multiplexer #(.select(4), .width(2)) multiplexer_3 (
    .in0(decode_1_pin_3to2), .in1(decode_1_pin_3to2), .in2(decode_1_pin_3to2), .in3(2'b00), .in4(2'b00),
    .in5(2'b00), .in6(2'b00), .in7(2'b00), .in8(2'b00), .in9(2'b00), .in10(2'b00), .in11(decode_1_pin_5to4),
    .in12(2'b00), .in13(2'b00), .in14(2'b00), .in15(2'b00), .out(Rs2), .sel(decode_1_pin_bto8));
  not not_1 (not_1_out, comparator_4_gt);
  and and_1 (is_nop, comparator_1_eq, comparator_2_eq);
  not not_2 (is_rd, comparator_3_gt);
  or or_1 (or_1_out, not_1_out, comparator_5_eq);
  nand nand_1 (nand_1_out, comparator_6_eq, comparator_7_eq);
  and and_2 (is_rs2, or_1_out, nand_1_out);
endmodule

module Forwarding_Unit (
  input  [11:0] EX_IR,
  input  [11:0] MEM_IR,
  input  [11:0] WB_IR,
  input  [11:0] MEM_Res,
  input  [11:0] WB_Res,
  output [11:0] A,
  output A_EN,
  output [11:0] B,
  output B_EN
);

  wire and_1_out, comparator_1_eq, comparator_2_eq, comparator_3_eq, comparator_4_gt, comparator_5_eq,
       comparator_6_eq, comparator_7_eq, comparator_8_eq, comparator_9_eq, nand_1_out, nor_2_out, or_1_out;
  wire [1:0] decode_1_pin_1to0, decode_1_pin_3to2, decode_1_pin_5to4, decode_1_pin_7to6, decode_2_pin_7to6,
       decode_3_pin_7to6, multiplexer_1_out, multiplexer_2_out, multiplexer_3_out, multiplexer_4_out,
       nor_1_out, transistor_1_out, transistor_2_out;
  wire [3:0] decode_1_pin_bto8, decode_2_pin_bto8, decode_3_pin_bto8;
  wire [11:0] nand_2_out, transistor_4_out, transistor_5_out;

  decode decode_1 (
    .Instruction(EX_IR), .PIN_Bto8(decode_1_pin_bto8), .PIN_7to6(decode_1_pin_7to6),
    .PIN_5to4(decode_1_pin_5to4), .PIN_3to2(decode_1_pin_3to2), .PIN_1to0(decode_1_pin_1to0));  // open: PIN_5to0, PIN_3to0
  decode decode_2 (
    .Instruction(MEM_IR), .PIN_Bto8(decode_2_pin_bto8), .PIN_7to6(decode_2_pin_7to6));  // open: PIN_5to4, PIN_5to0, PIN_3to2, PIN_3to0, PIN_1to0
  decode decode_3 (
    .Instruction(WB_IR), .PIN_Bto8(decode_3_pin_bto8), .PIN_7to6(decode_3_pin_7to6));  // open: PIN_5to4, PIN_5to0, PIN_3to2, PIN_3to0, PIN_1to0
  Multiplexer #(.select(4), .width(2)) multiplexer_1 (
    .in1(decode_1_pin_5to4), .in2(decode_1_pin_5to4), .in3(decode_1_pin_5to4), .in4(decode_1_pin_5to4),
    .in5(decode_1_pin_5to4), .in6(decode_1_pin_5to4), .in7(decode_1_pin_5to4), .in8(decode_1_pin_5to4),
    .in9(decode_1_pin_5to4), .in10(decode_1_pin_5to4), .in11(decode_1_pin_5to4), .in12(decode_1_pin_5to4),
    .in14(decode_1_pin_7to6), .in15(decode_1_pin_7to6), .out(multiplexer_1_out), .sel(decode_1_pin_bto8));  // open: in0, in13
  Multiplexer #(.select(4), .width(2)) multiplexer_2 (
    .in1(decode_2_pin_7to6), .in2(decode_2_pin_7to6), .in3(decode_2_pin_7to6), .in4(decode_2_pin_7to6),
    .in5(decode_2_pin_7to6), .in6(decode_2_pin_7to6), .in7(decode_2_pin_7to6), .in8(decode_2_pin_7to6),
    .in9(decode_2_pin_7to6), .in10(decode_2_pin_7to6), .in11(decode_2_pin_7to6), .in12(decode_2_pin_7to6),
    .in13(decode_2_pin_7to6), .out(multiplexer_2_out), .sel(decode_2_pin_bto8));  // open: in0, in14, in15
  Multiplexer #(.select(4), .width(2)) multiplexer_3 (
    .in1(decode_3_pin_7to6), .in2(decode_3_pin_7to6), .in3(decode_3_pin_7to6), .in4(decode_3_pin_7to6),
    .in5(decode_3_pin_7to6), .in6(decode_3_pin_7to6), .in7(decode_3_pin_7to6), .in8(decode_3_pin_7to6),
    .in9(decode_3_pin_7to6), .in10(decode_3_pin_7to6), .in11(decode_3_pin_7to6), .in12(decode_3_pin_7to6),
    .in13(decode_3_pin_7to6), .out(multiplexer_3_out), .sel(decode_3_pin_bto8));  // open: in0, in14, in15
  Multiplexer #(.select(4), .width(2)) multiplexer_4 (
    .in0(decode_1_pin_3to2), .in1(decode_1_pin_3to2), .in2(decode_1_pin_3to2), .out(multiplexer_4_out),
    .sel(decode_1_pin_bto8));  // open: in3, in4, in5, in6, in7, in8, in9, in10, in11, in12, in13, in14, in15
  Transistor #(.width(2)) transistor_1 (.in(multiplexer_4_out), .out(transistor_1_out), .gate(nor_1_out));
  Comparator #(.width(12)) comparator_1 (.a(EX_IR), .b({12{1'b0}}), .eq(comparator_1_eq));  // open: gt, lt
  Comparator #(.width(2)) comparator_2 (.a(decode_1_pin_1to0), .b(2'b11), .eq(comparator_2_eq));  // open: gt, lt
  Comparator #(.width(4)) comparator_3 (.a(decode_1_pin_bto8), .b(4'b0010), .eq(comparator_3_eq));  // open: gt, lt
  Comparator #(.width(4)) comparator_4 (.a(decode_1_pin_bto8), .b(4'b0010), .gt(comparator_4_gt));  // open: eq, lt
  Comparator #(.width(4)) comparator_5 (.a(decode_1_pin_bto8), .b(4'b1101), .eq(comparator_5_eq));  // open: gt, lt
  Transistor #(.width(2)) transistor_2 (.in(multiplexer_1_out), .out(transistor_2_out), .gate(nor_2_out));
  and and_1 (and_1_out, comparator_2_eq, comparator_3_eq);
  Comparator #(.width(2)) comparator_6 (
    .a(transistor_2_out), .b(multiplexer_2_out), .eq(comparator_6_eq));  // open: gt, lt
  Comparator #(.width(2)) comparator_7 (
    .a(transistor_1_out), .b(multiplexer_2_out), .eq(comparator_7_eq));  // open: gt, lt
  Comparator #(.width(2)) comparator_8 (
    .a(transistor_2_out), .b(multiplexer_3_out), .eq(comparator_8_eq));  // open: gt, lt
  Comparator #(.width(2)) comparator_9 (
    .a(transistor_1_out), .b(multiplexer_3_out), .eq(comparator_9_eq));  // open: gt, lt
  or or_1 (or_1_out, and_1_out, comparator_4_gt);
  nand nand_1 (nand_1_out, comparator_8_eq, comparator_6_eq);
  xor xor_1 (A_EN, comparator_6_eq, comparator_8_eq);
  xor xor_2 (B_EN, comparator_7_eq, comparator_9_eq);
  nand nand_2 (nand_2_out[0], comparator_7_eq, comparator_9_eq);
  Transistor #(.width(12)) transistor_3 (.in(WB_Res), .out(A), .gate(comparator_8_eq));
  nor nor_1 (nor_1_out[0], comparator_1_eq, or_1_out);
  nor nor_2 (nor_2_out, comparator_1_eq, comparator_5_eq);
  Transistor #(.width(12)) transistor_4 (.in(MEM_Res), .out(transistor_4_out), .gate(comparator_6_eq));
  Transistor #(.width(12)) transistor_5 (.in(MEM_Res), .out(transistor_5_out), .gate(comparator_7_eq));
  Transistor #(.width(12)) transistor_6 (.in(transistor_4_out), .out(A), .gate(nand_1_out));
  Transistor #(.width(12)) transistor_7 (.in(transistor_5_out), .out(B), .gate(nand_2_out));
  Transistor #(.width(12)) transistor_8 (.in(WB_Res), .out(B), .gate(comparator_9_eq));
  // Pins of 1 and 12 bits meet at nand_2_out
  // Pins of 1 and 2 bits meet at nor_1_out

  // Notes on the sheet:
  //   No RS2
  //   No RS1
endmodule

module Forwarding_unitV2 (
  input  [11:0] EX_IR,
  input  [11:0] MEM_IR,
  input  [11:0] WB_IR,
  output [1:0] A,
  output [1:0] B
);

  wire and_1_out, and_2_out, and_3_out, and_4_out, and_5_out, and_6_out, and_7_out, and_8_out, and_9_out,
       comparator_1_eq, comparator_2_eq, comparator_3_eq, comparator_4_eq, comparator_5_gt, comparator_6_eq,
       comparator_7_eq, comparator_8_eq, comparator_9_eq, comparator_10_eq, nor_2_out, or_1_out, or_2_out,
       or_3_out, xor_1_out, xor_2_out;
  wire [1:0] decode_1_pin_1to0, decode_1_pin_3to2, decode_1_pin_5to4, decode_1_pin_7to6, decode_2_pin_7to6,
       decode_3_pin_7to6, multiplexer_1_out, multiplexer_2_out, multiplexer_3_out, multiplexer_4_out,
       nor_1_out, transistor_1_out, transistor_2_out;
  wire [3:0] decode_1_pin_bto8, decode_2_pin_bto8, decode_3_pin_bto8;

  decode decode_1 (
    .Instruction(EX_IR), .PIN_Bto8(decode_1_pin_bto8), .PIN_7to6(decode_1_pin_7to6),
    .PIN_5to4(decode_1_pin_5to4), .PIN_3to2(decode_1_pin_3to2), .PIN_1to0(decode_1_pin_1to0));  // open: PIN_5to0, PIN_3to0
  decode decode_2 (
    .Instruction(MEM_IR), .PIN_Bto8(decode_2_pin_bto8), .PIN_7to6(decode_2_pin_7to6));  // open: PIN_5to4, PIN_5to0, PIN_3to2, PIN_3to0, PIN_1to0
  decode decode_3 (
    .Instruction(WB_IR), .PIN_Bto8(decode_3_pin_bto8), .PIN_7to6(decode_3_pin_7to6));  // open: PIN_5to4, PIN_5to0, PIN_3to2, PIN_3to0, PIN_1to0
  Multiplexer #(.select(4), .width(2)) multiplexer_1 (
    .in1(decode_1_pin_5to4), .in2(decode_1_pin_5to4), .in3(decode_1_pin_5to4), .in4(decode_1_pin_5to4),
    .in5(decode_1_pin_5to4), .in6(decode_1_pin_5to4), .in7(decode_1_pin_5to4), .in8(decode_1_pin_5to4),
    .in9(decode_1_pin_5to4), .in10(decode_1_pin_5to4), .in11(decode_1_pin_5to4), .in12(decode_1_pin_5to4),
    .in14(decode_1_pin_7to6), .in15(decode_1_pin_7to6), .out(multiplexer_1_out), .sel(decode_1_pin_bto8));  // open: in0, in13
  Multiplexer #(.select(4), .width(2)) multiplexer_2 (
    .in1(decode_2_pin_7to6), .in2(decode_2_pin_7to6), .in3(decode_2_pin_7to6), .in4(decode_2_pin_7to6),
    .in5(decode_2_pin_7to6), .in6(decode_2_pin_7to6), .in7(decode_2_pin_7to6), .in8(decode_2_pin_7to6),
    .in9(decode_2_pin_7to6), .in10(decode_2_pin_7to6), .in11(decode_2_pin_7to6), .in12(decode_2_pin_7to6),
    .in13(decode_2_pin_7to6), .out(multiplexer_2_out), .sel(decode_2_pin_bto8));  // open: in0, in14, in15
  Multiplexer #(.select(4), .width(2)) multiplexer_3 (
    .in1(decode_3_pin_7to6), .in2(decode_3_pin_7to6), .in3(decode_3_pin_7to6), .in4(decode_3_pin_7to6),
    .in5(decode_3_pin_7to6), .in6(decode_3_pin_7to6), .in7(decode_3_pin_7to6), .in8(decode_3_pin_7to6),
    .in9(decode_3_pin_7to6), .in10(decode_3_pin_7to6), .in11(decode_3_pin_7to6), .in12(decode_3_pin_7to6),
    .in13(decode_3_pin_7to6), .out(multiplexer_3_out), .sel(decode_3_pin_bto8));  // open: in0, in14, in15
  Multiplexer #(.select(4), .width(2)) multiplexer_4 (
    .in0(decode_1_pin_3to2), .in1(decode_1_pin_3to2), .in2(decode_1_pin_3to2), .out(multiplexer_4_out),
    .sel(decode_1_pin_bto8));  // open: in3, in4, in5, in6, in7, in8, in9, in10, in11, in12, in13, in14, in15
  Transistor #(.width(2)) transistor_1 (.in(multiplexer_4_out), .out(transistor_1_out), .gate(nor_1_out));
  Comparator #(.width(4)) comparator_1 (.a(decode_3_pin_bto8), .b(4'b1010), .eq(comparator_1_eq));  // open: gt, lt
  Comparator #(.width(12)) comparator_2 (.a(EX_IR), .b({12{1'b0}}), .eq(comparator_2_eq));  // open: gt, lt
  Comparator #(.width(2)) comparator_3 (.a(decode_1_pin_1to0), .b(2'b11), .eq(comparator_3_eq));  // open: gt, lt
  Comparator #(.width(4)) comparator_4 (.a(decode_1_pin_bto8), .b(4'b0010), .eq(comparator_4_eq));  // open: gt, lt
  Comparator #(.width(4)) comparator_5 (.a(decode_1_pin_bto8), .b(4'b0010), .gt(comparator_5_gt));  // open: eq, lt
  Comparator #(.width(4)) comparator_6 (.a(decode_1_pin_bto8), .b(4'b1101), .eq(comparator_6_eq));  // open: gt, lt
  Transistor #(.width(2)) transistor_2 (.in(multiplexer_1_out), .out(transistor_2_out), .gate(nor_2_out));
  and and_1 (and_1_out, comparator_3_eq, comparator_4_eq);
  Comparator #(.width(2)) comparator_7 (
    .a(transistor_2_out), .b(multiplexer_2_out), .eq(comparator_7_eq));  // open: gt, lt
  Comparator #(.width(2)) comparator_8 (
    .a(transistor_1_out), .b(multiplexer_2_out), .eq(comparator_8_eq));  // open: gt, lt
  Comparator #(.width(2)) comparator_9 (
    .a(transistor_2_out), .b(multiplexer_3_out), .eq(comparator_9_eq));  // open: gt, lt
  Comparator #(.width(2)) comparator_10 (
    .a(transistor_1_out), .b(multiplexer_3_out), .eq(comparator_10_eq));  // open: gt, lt
  or or_1 (or_1_out, and_1_out, comparator_5_gt);
  xor xor_1 (xor_1_out, comparator_7_eq, comparator_9_eq);
  xor xor_2 (xor_2_out, comparator_10_eq, comparator_8_eq);
  nor nor_1 (nor_1_out[0], comparator_2_eq, or_1_out);
  nor nor_2 (nor_2_out, comparator_2_eq, comparator_6_eq);
  and and_2 (and_2_out, xor_1_out, comparator_7_eq);
  and and_3 (and_3_out, comparator_7_eq, comparator_9_eq);
  and and_4 (and_4_out, comparator_8_eq, comparator_10_eq);
  and and_5 (and_5_out, xor_1_out, comparator_9_eq);
  and and_6 (and_6_out, comparator_1_eq, comparator_9_eq);
  and and_7 (and_7_out, comparator_10_eq, comparator_1_eq);
  and and_8 (and_8_out, comparator_10_eq, xor_2_out);
  and and_9 (and_9_out, comparator_8_eq, xor_2_out);
  or or_2 (or_2_out, and_3_out, and_5_out);
  or or_3 (or_3_out, and_4_out, and_9_out);
  Transistor #(.width(2)) transistor_3 (.in(2'b01), .out(A), .gate(and_2_out));
  Transistor #(.width(2)) transistor_4 (.in(2'b10), .out(A), .gate(or_2_out));
  Transistor #(.width(2)) transistor_5 (.in(2'b11), .out(A), .gate(and_6_out));
  Transistor #(.width(2)) transistor_6 (.in(2'b11), .out(B), .gate(and_7_out));
  Transistor #(.width(2)) transistor_7 (.in(2'b01), .out(B), .gate(and_8_out));
  Transistor #(.width(2)) transistor_8 (.in(2'b10), .out(B), .gate(or_3_out));
  // Pins of 1 and 2 bits meet at nor_1_out

  // Notes on the sheet:
  //   Load
  //   A
  //   B
  //   A
  //   B
  //   MEM A
  //   WB A
  //   WB B
  //   WB A
  //   LD A
  //   LD B
  //   No RS2
  //   No RS1
  //   MEM A
  //   MEM B
endmodule
